// Logisim project login sistemas.circ as structural Verilog: 1 circuit, main circuit main
module main (
  input  [7:0] in_1,
  input  [7:0] in_2,
  input  [3:0] in_3,
  input  [7:0] in_4,
  input  [2:0] in_5,
  input  A,
  input  in_7,
  input  A_2,
  input  B,
  input  in_10,
  input  in_11,
  input  in_12,
  input  in_13
);

  wire and_1_out, and_2_out, and_3_out, and_4_out, and_5_out, and_6_out, bitselector_1_out, clock_1_out,
       decoder_1_out0, decoder_1_out5, decoder_1_out10, decoder_1_out14, j_k_ff_1_q, j_k_ff_2_q, j_k_ff_3_q,
       j_k_ff_4_q, nor_1_out, not_2_out, not_3_out, or_1_out, or_2_out, xor_1_out, xor_2_out, xor_3_out,
       xor_4_out;
  wire [7:0] adder_1_out, adder_2_out, not_1_out;

  Hex_Digit_Display hex_digit_display_1 (.value(in_3));  // open: dp
  Decoder #(.select(4)) decoder_1 (
    .out0(decoder_1_out0), .out5(decoder_1_out5), .out10(decoder_1_out10), .out14(decoder_1_out14), .sel(in_3));  // open: out1, out2, out3, out4, out6, out7, out8, out9, out11, out12, out13, out15, en
  BitSelector bitselector_1 (.in(in_4), .out(bitselector_1_out), .sel(in_5));
  // Probe on bitselector_1_out
  xor xor_1 (xor_1_out, A, in_7);
  and and_1 (and_1_out, A, in_7);
  or or_1 (or_1_out, decoder_1_out0, decoder_1_out5, decoder_1_out10, decoder_1_out14);
  // Probe on xor_1_out
  // Probe on and_1_out
  xor xor_2 (xor_2_out, in_10, in_11);
  and and_2 (and_2_out, in_10, in_11);
  LED led_1 (.in(or_1_out));
  xor xor_3 (xor_3_out, in_12, in_13);
  and and_3 (and_3_out, in_12, in_13);
  // Probe on xor_2_out
  // Probe on and_2_out
  and and_4 (and_4_out, xor_3_out, and_2_out);
  Clock clock_1 (.out(clock_1_out));
  // Probe on xor_4_out
  xor xor_4 (xor_4_out, xor_3_out, and_2_out);
  assign not_1_out = ~in_2;  // NOT_Gate not_1, 8 bits wide
  J_K_Flip_Flop j_k_ff_1 (.clk(clock_1_out), .K(clock_1_out), .Q(j_k_ff_1_q));  // open: J, Qn, preset, en, reset
  not not_2 (not_2_out, A_2);
  not not_3 (not_3_out, A_2);
  or or_2 (or_2_out, and_4_out, and_3_out);
  J_K_Flip_Flop j_k_ff_2 (.clk(j_k_ff_1_q), .K(clock_1_out), .Q(j_k_ff_2_q));  // open: J, Qn, preset, en, reset
  nor nor_1 (nor_1_out, A_2, A_2);
  and and_5 (and_5_out, A_2, not_2_out);
  and and_6 (and_6_out, not_3_out, A_2);
  // Probe on or_2_out
  Adder adder_1 (.a(not_1_out), .b(8'h1), .out(adder_1_out));  // open: cin, cout
  J_K_Flip_Flop j_k_ff_3 (
    .J(clock_1_out), .clk(j_k_ff_2_q), .K(clock_1_out), .Q(j_k_ff_3_q));  // open: Qn, preset, en, reset
  // Probe on nor_1_out
  // Probe on and_5_out
  // Probe on and_6_out
  // Probe on adder_2_out
  Adder adder_2 (.a(in_1), .b(adder_1_out), .out(adder_2_out));  // open: cin, cout
  J_K_Flip_Flop j_k_ff_4 (
    .J(clock_1_out), .clk(j_k_ff_3_q), .K(clock_1_out), .Q(j_k_ff_4_q));  // open: Qn, preset, en, reset
  // Probe on j_k_ff_4_q
  // Probe on j_k_ff_1_q
  // Probe on j_k_ff_3_q
  // Probe on j_k_ff_2_q

  assign B = A_2;

  // Notes on the sheet:
  //   Resultado
  //   Acarreo
  //   Comparador
  //   Resultado
  //   Acarreo
  //   A=B
  //   A>B
  //   A<B
endmodule
